# Fritzing sketch MQTT-Gateway-Design (saved by Fritzing 0.9.3b)

parts:
  Bauteil1 = Arduino Mega 2560 (Rev3)
  Bauteil2 = Arduino Ethernet Shield (Rev3)
  Bauteil3 = NRF24L01+ Breakout Board

nets:
  N1: Bauteil1.D50, Bauteil3.MISO
  N2: Bauteil1.D51, Bauteil3.MOSI
  N3: Bauteil1.D52, Bauteil3.SCK
  N4: Bauteil2.D8, Bauteil3.CS
  N5: Bauteil2.D7, Bauteil3.CE
  3V3: Bauteil2.3V3, Bauteil3.VCC
  GND: Bauteil2.GND, Bauteil3.GND
