# Fritzing sketch Sensor-Design (saved by Fritzing 0.9.3b)
stripboards: 1

parts:
  U1 = ESP32-38PinWide [part_number=ESP32-38PinWide]
  Bauteil1 = NRF24L01+ Breakout Board
  DHT1 = DHT22 Humidity and Temperature Sensor
  Chirp!_Soil_Moisture_Sensor1 = Chirp! Soil Moisture Sensor v2.7.3

nets:
  N1: U1.GPIO36, Bauteil1.CE
  N2: U1.GPIO39, Bauteil1.CS
  N3: U1.GPIO34, DHT1.DATA
  GND: U1.GPIO9, Bauteil1.GND, DHT1.GND, Chirp!_Soil_Moisture_Sensor1.pin_2
  VCC: U1.GPIO11, Bauteil1.VCC, DHT1.VDD, Chirp!_Soil_Moisture_Sensor1.Pin_1
  N4: U1.GPIO15, Chirp!_Soil_Moisture_Sensor1.Pin_0
  N5: U1.GPIO17, Bauteil1.MISO
  N6: U1.GPIO5, Bauteil1.MOSI
  N7: U1.GPIO18, Bauteil1.SCK

custom parts:
  ESP32-38PinWide: Generic 38-Pin ESP32 with wide format (only access to one side of pins on a breadboard) based on Stephen Lilley's HiLetgo ESP-WROOM-32 ESP32 ESP-32S Development Board.
